# Fritzing sketch lcd (saved by Fritzing 0.7.11b)
breadboards: 1

parts:
  LCD1 = LCD screen
  Launchpad1 = TI Launchpad MSP430G2
  R2 = Resistor [tolerance=±5% resistance=22k package=THT]
  R3 = Photocell (LDR) [package=THT]
  R4 = Trimmer Potentiometer [maximum_resistance=10kΩ package=THT]

nets:
  N1: LCD1.VSS, R2.Pin_1, R4.leg1
  N2: LCD1.VDD, Launchpad1.p1
  N3: LCD1.V0, R4.wiper
  N4: LCD1.RS, Launchpad1.p15
  N5: LCD1.R/W, Launchpad1.p20
  N6: LCD1.E, Launchpad1.p14
  N7: LCD1.DB6, Launchpad1.p2
  N8: LCD1.DB7, Launchpad1.p3
  N9: LCD1.LED+, Launchpad1.p4
  N10: LCD1.LED-, Launchpad1.p5
  N11: Launchpad1.p6, R2.Pin_0, R3.pin_1
